# Fritzing sketch Transformation (saved by Fritzing 0.9.3b)
breadboards: 1

parts:
  Part1 = Arduino Uno (Rev3)
  IR1 = TSOP312.., 314.. [package=THT]
  M2 = DC Motor
  VCC1 = 4 x AAA Battery Mount
  M3 = Dagu DGServo 9g (Top view) [part_number=RS001B]
  LED1 = LED - 5mm [color="Red (633nm)" package="5 mm [THT]"]

nets:
  N1: Part1.A2, M3.pulse
  GND: Part1.GND, IR1.Vs, M3.gnd, LED1.cathode
  N2: Part1.D5_PWM, IR1.GND
  N3: Part1.D6_PWM, LED1.anode
  N4: Part1.3V3, IR1.Data
  5V: Part1.5V, M3.vcc
  N5: M2.pin_1, VCC1.+

notes:
  Couldn't find a correct relay, so here's a description:
  Black wire from socket to NC. Battery pack ground to the middle screw terminal. Arduino pin 13 to S. Arduino 5V(from breadboard) to +, and Arduino Gnd to -. The red wire directly connects to the motor.
  Not actually spaced like this
  This represents the LED string.
